# Fritzing sketch MainSketch (saved by Fritzing 0.9.3b)

parts:
  Q1 = Basic FET N-Channel [package="D2Pak [SMD]"]
  R1 = Photocell (LDR) [package=THT]
  TP1 = TP4056 [chip_label=TP4056 package="DIP (Dual Inline) [THT]"]
  Part1 = Lithium Ion Polymer Battery 3.7v 500mAh [part_number=1578]
  S1 = Toggle Switch spst [package=THT]
  U1 = ESP8266 ESP-01 Upgraded WiFi Module [part_number=ESP8266]
  RGB_SMD_LED1 = SMD RGB LED (WS2812B) [package=5050]
  R2 = Resistor [tolerance=±5% resistance=220 package="1206 [SMD]"]
  RGB_SMD_LED2 = SMD RGB LED (WS2812B) [package=5050]
  RGB_SMD_LED3 = SMD RGB LED (WS2812B) [package=5050]
  RGB_SMD_LED4 = SMD RGB LED (WS2812B) [package=5050]
  RGB_SMD_LED5 = SMD RGB LED (WS2812B) [package=5050]

nets:
  N1: Q1.Gate, R1.pin_1, R2.Pin_0
  VSS: Q1.source, TP1.pin6, U1.GND, RGB_SMD_LED1.VSS, R2.Pin_1, RGB_SMD_LED2.VSS, RGB_SMD_LED3.VSS, RGB_SMD_LED4.VSS, RGB_SMD_LED5.VSS
  VDD: R1.pin_0, S1.COM, U1.VCC, U1.CH_PD, U1.TXD, RGB_SMD_LED1.VDD, RGB_SMD_LED2.VDD, RGB_SMD_LED3.VDD, RGB_SMD_LED4.VDD, RGB_SMD_LED5.VDD
  N2: TP1.pin3, S1.L1
  N3: TP1.pin4, Part1.positive
  N4: TP1.pin5, Part1.negative
  N5: U1.GPIO_2, RGB_SMD_LED1.DIN
  N6: RGB_SMD_LED1.DOUT, RGB_SMD_LED2.DIN
  N7: RGB_SMD_LED2.DOUT, RGB_SMD_LED3.DIN
  N8: RGB_SMD_LED3.DOUT, RGB_SMD_LED4.DIN
  N9: RGB_SMD_LED4.DOUT, RGB_SMD_LED5.DIN

notes:
  VCC On The Ultrasonic Module
  GND On The Ultrasonic Module

custom parts:
  TP4056: A DIP stand-in part for whatever IC you want. With 6 pins on a 300mil dual inline package (DIP) footprint.
  Lithium Ion Polymer Battery 3.7v 500mAh: Lithium ion polymer (also known as 'lipo' or 'lipoly') batteries are thin, light and powerful. The output ranges from 4.2V when completely charged to 3.7V. This battery has a capacity of 500mAh for a total of about 1.9 Wh. The batteries come pre-attached with a genuine 2-pin JST-PH connector as shown and include the necessary protection circuitry.
  Toggle Switch spst: Toggle Switch single pole single throw
  ESP8266 ESP-01 Upgraded WiFi Module: Upgraded Version ESP-01,all Flash are upgraded to 1M byte.Also support Cloud service remote transmission.
  SMD RGB LED (WS2812B): The WS2812B is an RGB LED with a WS2811 control IC built right into the LED. Its improvement over its WS2812 ancestor is the reduction to 4 pins (a single power supply instead of 2) and dropping the requirement for the external resistors. The manufacturer says it has a better reverse connect protection.
