# Fritzing sketch firmware_Uplaod (saved by Fritzing 0.9.3b)

parts:
  Part1 = Arduino Uno (Rev3)
  U1 = ESP8266 ESP-01 Upgraded WiFi Module [part_number=ESP8266]

nets:
  GND: Part1.GND, Part1.RESET, U1.GPIO_0, U1.GND
  N1: Part1.D0/RX, U1.RXD
  N2: Part1.D1/TX, U1.TXD
  3V3: Part1.3V3, U1.VCC, U1.CH_PD

notes:
  RESET WIRE

custom parts:
  ESP8266 ESP-01 Upgraded WiFi Module: Upgraded Version ESP-01,all Flash are upgraded to 1M byte.Also support Cloud service remote transmission.
